# Fritzing sketch lampadamagica (saved by Fritzing 0.9.3b)
breadboards: 1

parts:
  Arduino1 = Arduino Mini (Rev5)
  S1 = Pushbutton [package="[THT]"]  # not connected
  S2 = Pushbutton [package="[THT]"]
  S3 = Pushbutton [package="[THT]"]  # not connected
  R1 = Resistor [tolerance=±5% resistance=120 package="1206 [SMD]"]  # not connected
  R2 = Resistor [tolerance=±5% resistance=120 package="1206 [SMD]"]  # not connected
  R3 = Resistor [tolerance=±5% resistance=120 package="1206 [SMD]"]
  R5 = Resistor [tolerance=±5% resistance=10k package="1206 [SMD]"]
  R6 = Resistor [tolerance=±5% resistance=10k package="1206 [SMD]"]
  R7 = Resistor [tolerance=±5% resistance=33 package="1206 [SMD]"]
  R8 = Resistor [tolerance=±5% resistance=22 package="1206 [SMD]"]
  R9 = Resistor [tolerance=±5% resistance=15 package="1206 [SMD]"]
  R4 = Resistor [tolerance=±5% resistance=10k package="1206 [SMD]"]
  R10 = Resistor [tolerance=±5% resistance=15 package="1206 [SMD]"]
  R11 = Resistor [tolerance=±5% resistance=120 package="1206 [SMD]"]
  Q1 = NPN-Transistor [package="TO92 [THT]"]
  Q2 = NPN-Transistor [package="TO92 [THT]"]
  Q3 = NPN-Transistor [package="TO92 [THT]"]
  Q4 = NPN-Transistor [package="TO92 [THT]"]

nets:
  N1: Arduino1.GND, R5.Pin_1, R6.Pin_1, R4.Pin_1
  N2: Arduino1.5V, S2.Pin_3, S2.Pin_4, Q1.E, Q2.E, Q3.E, Q4.E
  N3: Arduino1.D11_PWM, R11.Pin_0
  N4: Arduino1.D10_PWM, R3.Pin_0
  N5: S2.Pin_1, S2.Pin_2, R5.Pin_0
  N6: R3.Pin_1, Q3.B
  N7: R7.Pin_1, Q1.C
  N8: R8.Pin_1, Q2.C
  N9: R9.Pin_1, Q3.C
  N10: R10.Pin_1, Q4.C
  N11: R11.Pin_1, Q4.B
